# Fritzing sketch pump (saved by Fritzing 0.9.3b)
breadboards: 1

parts:
  Q1 = MOSFET-NCHANNEL [package=to220v]
  Part1 = Arduino Uno (Rev3)
  M1 = DC Motor

nets:
  N1: Q1.G, Part1.GND
  N2: Q1.D, Part1.D8
  N3: Q1.S, M1.pin_2
  N4: Part1.5V, M1.pin_1
